// Logisim project timer_.circ as structural Verilog: 2 circuits, main circuit main
module main (
  input  [3:0] boutons,
  input  [2:0] etat,
  input  [22:0] temps,
  output [22:0] temps_restant,
  output sonne
);

  wire actif_q, and_1_out, and_2_out, comparator_1_eq, comparator_2_eq, or_1_out, subtractor_1_bout;
  wire [22:0] adder_1_out, duree_q, fin_q, multiplexer_1_out, subtractor_1_out, subtractor_2_out;

  Comparator #(.width(3), .mode("unsigned")) comparator_1 (.a(etat), .b(3'b011), .eq(comparator_1_eq));  // open: gt, lt
  and and_1 (and_1_out, boutons[2], comparator_1_eq);
  or or_1 (or_1_out, and_1_out, 1'b0);
  T_Flip_Flop actif (.T(comparator_1_eq), .clk(or_1_out), .Q(actif_q));  // open: Qn, reset, preset
  Register #(.width(23)) duree (.D(23'hbb8), .clk(comparator_1_eq), .Q(duree_q));  // open: en, clr
  and and_2 (and_2_out, boutons[2], actif_q);
  Register #(.width(23)) debut (.D(temps), .clk(and_2_out));  // open: en, Q, clr
  Adder #(.width(23)) adder_1 (.a(duree_q), .b(temps), .out(adder_1_out));  // open: cin, cout
  Subtractor #(.width(23)) subtractor_1 (
    .a(adder_1_out), .b(23'h5c4900), .out(subtractor_1_out), .bout(subtractor_1_bout));  // open: bin
  Register #(.width(23)) fin (.D(multiplexer_1_out), .clk(and_2_out), .Q(fin_q));  // open: en, clr
  Multiplexer #(.width(23), .enable("false")) multiplexer_1 (
    .in0(subtractor_1_out), .in1(adder_1_out), .out(multiplexer_1_out), .sel(subtractor_1_bout));
  Comparator #(.width(23), .mode("unsigned")) comparator_2 (
    .a(fin_q), .b(temps), .eq(comparator_2_eq));  // open: gt, lt
  and and_3 (sonne, comparator_2_eq, actif_q);
  Subtractor #(.width(23)) subtractor_2 (.a(fin_q), .b(temps), .out(subtractor_2_out));  // open: bin, bout
  Multiplexer #(.width(23), .enable("false")) multiplexer_2 (
    .in0(duree_q), .in1(subtractor_2_out), .out(temps_restant), .sel(actif_q));

  // Notes on the sheet:
  //   mode set
  //   incrémenter valeur du mode set 
  //   passer au segment suivant du set
  //   reset
  //   ne pas mettre de sortie, mais changer l'état à SONNE (100)
endmodule

module Timer (
  input  [3:0] Boutons,
  input  [2:0] Etat,
  input  [22:0] Temps
);

  wire comparator_1_eq;

  Comparator #(.width(3)) comparator_1 (.a(Etat), .b(3'b011), .eq(comparator_1_eq));  // open: gt, lt
endmodule
